# Fritzing sketch rpi (saved by Fritzing 0.9.0b)
breadboards: 1

parts:
  Raspberry_Pi_B_rev1 = Raspberry Pi B rev1
  R1 = Resistor [tolerance=±5% resistance=220 package=THT]
  LED1 = LED - 5mm [color="Red (633nm)" package="5 mm [THT]"]
  R2 = Resistor [package="0402 [SMD]"]
  LED2 = LED - 5mm [color="Red (633nm)" package="5 mm [THT]"]

nets:
  N1: Raspberry_Pi_B_rev1.GPIO_0, LED2.anode
  N2: Raspberry_Pi_B_rev1.GND, R1.Pin_0
  N3: Raspberry_Pi_B_rev1.GPIO_4, LED1.anode
  N4: R1.Pin_1, LED1.cathode
  N5: R2.Pin_1, LED2.cathode
